# Fritzing sketch analogIO (saved by Fritzing 1.0.5)
breadboards: 1

parts:
  M1 = ESP32-C3-DevKitM-1 [part_number=ESP32-C3-DevKitM-1]
  R1 = Resistor [tolerance=±5% power=0.25W resistance=220 package=THT]
  R2 = Photocell (LDR) [power=0.25W dark_resistance_@0.01lx=300kΩ light_resistance_@100lx=400Ω luminance=10lx package=THT]
  M2 = ESP32-C3-DevKitM-1 [part_number=ESP32-C3-DevKitM-1]
  R3 = 12mm Trimmer Potentiometer (Large) [maximum_resistance=10kΩ knob_status=50% power=0.5W package=THT]

nets:
  N1: M1.GND-1, M1.GND-4, M1.GND-9, M1.GND-12, M1.GND-15, M1.GND-16, M1.GND-21, M1.GND-23, M1.GND-27, M1.GND-30, R1.Pin_1
  N2: M1.3V3-17, M1.3V3-18, R2.pin_0
  N3: M1.2, R1.Pin_0, R2.pin_1
  N4: M1.5V-28, M1.5V-29
  N5: M2.GND-1, M2.GND-4, M2.GND-9, M2.GND-12, M2.GND-15, M2.GND-16, M2.GND-21, M2.GND-23, M2.GND-27, M2.GND-30, R3.leg2
  N6: M2.3V3-17, M2.3V3-18, R3.leg1
  N7: M2.2, R3.wiper
  N8: M2.5V-28, M2.5V-29

custom parts:
  ESP32-C3-DevKitM-1: The DOIT Esp32 DevKit v1 is one of the development board created by DOIT to evaluate the ESP-WROOM-32 module. It is based on the ESP32 microcontroller that boasts Wifi, Bluetooth, Ethernet and Low Power support all in a single chip. (vanepp) Feb 2021: converted to ESP32-C3-DevKitM-1. This chip is 30pins long (2 x15) and 11 pins width.
