# Fritzing sketch button_aht20_oled (saved by Fritzing 1.0.5)
breadboards: 1

parts:
  M1 = ESP32-C3-DevKitM-1 [part_number=ESP32-C3-DevKitM-1]
  S1 = 0.91 inch OLED I2C Display 128 x 32 Pixels
  S2 = Pushbutton [package="[THT]"]
  SHT1 = StrawberryLinux SHT25 Sensor module [package=DIP]

nets:
  VCC: M1.GND-1, M1.GND-4, M1.GND-9, M1.GND-12, M1.GND-15, M1.GND-16, M1.3V3-17, M1.3V3-18, M1.GND-21, M1.GND-23, M1.GND-27, M1.GND-30, S1.VCC, S2.Pin_1, S2.Pin_2, SHT1.VCC
  N1: M1.6, S1.SDA, SHT1.SDA
  N2: M1.7, S2.Pin_3, S2.Pin_4
  N3: M1.9, S1.SCL, SHT1.SCL
  N4: M1.5V-28, M1.5V-29
  GND: S1.GND, SHT1.GND

custom parts:
  ESP32-C3-DevKitM-1: The DOIT Esp32 DevKit v1 is one of the development board created by DOIT to evaluate the ESP-WROOM-32 module. It is based on the ESP32 microcontroller that boasts Wifi, Bluetooth, Ethernet and Low Power support all in a single chip. (vanepp) Feb 2021: converted to ESP32-C3-DevKitM-1. This chip is 30pins long (2 x15) and 11 pins width.
