# Fritzing sketch pwm (saved by Fritzing 1.0.5)
breadboards: 1

parts:
  M1 = ESP32-C3-DevKitM-1 [part_number=ESP32-C3-DevKitM-1]
  J1 = Piezo Speaker
  LED1 = smd LED [color="Red (633nm)" package="0603 [SMD]"]
  R1 = Resistor [tolerance=±5% resistance=220 package="0402 [SMD]"]

nets:
  N1: M1.GND-1, M1.GND-4, M1.GND-9, M1.GND-12, M1.GND-15, M1.GND-16, M1.GND-21, M1.GND-23, M1.GND-27, M1.GND-30, J1.pin1, R1.Pin_1
  N2: M1.3V3-17, M1.3V3-18
  N3: M1.3, J1.pin2, LED1.anode
  N4: M1.5V-28, M1.5V-29
  N5: LED1.cathode, R1.Pin_0

custom parts:
  ESP32-C3-DevKitM-1: The DOIT Esp32 DevKit v1 is one of the development board created by DOIT to evaluate the ESP-WROOM-32 module. It is based on the ESP32 microcontroller that boasts Wifi, Bluetooth, Ethernet and Low Power support all in a single chip. (vanepp) Feb 2021: converted to ESP32-C3-DevKitM-1. This chip is 30pins long (2 x15) and 11 pins width.
