# Fritzing sketch button_pullup_pulldown (saved by Fritzing 1.0.8)
breadboards: 1

parts:
  M1 = ESP32-C3-DevKitM-1 [part_number=ESP32-C3-DevKitM-1]
  S1 = Pushbutton [package="[THT]"]

nets:
  N1: M1.GND-1, M1.GND-4, M1.GND-9, M1.GND-12, M1.GND-15, M1.GND-16, M1.GND-21, M1.GND-23, M1.GND-27, M1.GND-30, S1.Pin_3, S1.Pin_4
  N2: M1.3V3-17, M1.3V3-18
  N3: M1.2, S1.Pin_1, S1.Pin_2
  N4: M1.5V-28, M1.5V-29

custom parts:
  ESP32-C3-DevKitM-1: The DOIT Esp32 DevKit v1 is one of the development board created by DOIT to evaluate the ESP-WROOM-32 module. It is based on the ESP32 microcontroller that boasts Wifi, Bluetooth, Ethernet and Low Power support all in a single chip. (vanepp) Feb 2021: converted to ESP32-C3-DevKitM-1. This chip is 30pins long (2 x15) and 11 pins width.
